# Fritzing sketch rc-car-lights (saved by Fritzing 1.0.4)
circuit board: 8.46667cm x 5.64444cm
breadboards: 1

parts:
  U1 = 74HC595 [package="DIP16 [THT]"]
  Part1 = Arduino Uno (Rev3) - ICSP
  R1 = Resistor [tolerance=±5% power=0.25W resistance=220 package=THT]
  LED1 = LED - 5mm [color="White (4500K)" current=0.030A package="5 mm [THT]"]

nets:
  N1: U1.Q1, R1.Pin_1
  N2: Part1.GND, LED1.anode
  N3: R1.Pin_0, LED1.cathode
